# Fritzing sketch CNC3.0_schematic_V0.2 (saved by Fritzing 0.9.3b)

parts:
  LED1 = LED - 5mm [color="Red (633nm)" package="5 mm [THT]"]  # not connected
  C1 = Electrolytic Capacitor [capacitance=47µF package="100 mil [THT, electrolytic]"]
  C2 = Electrolytic Capacitor [capacitance=47µF package="100 mil [THT, electrolytic]"]

nets:
  N1: C1.-, C2.-

notes:
  Laser dot
  +5v
  Power
  PWM laser
  Enable
  LASER-
  on top
  EndStop
  Security Sys
  All closed = ON
  Implementation, top cover
  Water sensor
  X-motor
  Y-motor
  0.45uF
