# Fritzing sketch Driver (saved by Fritzing 0.9.3b)
breadboards: 2

parts:
  Pololu_A1 = Pololu A4988 [package=SO16]
  Pololu_A2 = Pololu A4988 [package=SO16]
  U1 = Optocoupler [package=THT]
  U2 = Optocoupler [package=THT]
  U3 = Optocoupler [package=THT]
  U4 = Optocoupler [package=THT]
  R1 = Resistor [tolerance=±5% resistance=10k package=THT]
  R2 = Resistor [tolerance=±5% resistance=10k package=THT]
  R3 = Resistor [tolerance=±5% resistance=10k package=THT]
  R4 = Resistor [tolerance=±5% resistance=10k package=THT]
  R5 = Resistor [tolerance=±5% resistance=330 package=THT]
  R6 = Resistor [tolerance=±5% resistance=330 package=THT]
  R7 = Resistor [tolerance=±5% resistance=330 package=THT]
  R8 = Resistor [tolerance=±5% resistance=330 package=THT]
  Part1 = Arduino Uno (Rev3)
  C1 = Electrolytic Capacitor [capacitance=0.1nF voltage=50V package="100 mil [THT, electrolytic]"]  # not connected
  Power_plug1 = Power plug
  M1 = Stepper Motor - Bipolar
  M2 = Stepper Motor - Bipolar
  S1 = Pushbutton [package=THT]
  S2 = Pushbutton [package=THT]
  R9 = Resistor [tolerance=±5% resistance=3.3k package=THT]
  U5 = mystery part, 3 pins [chip_label=BOX]
  S3 = Pushbutton [package=THT]
  R12 = Resistor [tolerance=±5% resistance=10k package=THT]
  C2 = Electrolytic Capacitor [capacitance=0.1nF voltage=50V package="100 mil [THT, electrolytic]"]
  R11 = Resistor [tolerance=±5% resistance=3.3k package=THT]
  R10 = Resistor [tolerance=±5% resistance=3.3k package=THT]
  R13 = Resistor [tolerance=±5% resistance=330 package=THT]
  R14 = Resistor [tolerance=±5% resistance=330 package=THT]
  C4 = Ceramic Capacitor [capacitance=100nF package="100 mil [THT, multilayer]"]
  C3 = Ceramic Capacitor [capacitance=100nF package="100 mil [THT, multilayer]"]
  U6 = Voltage Regulator - 5V [package="TO220 [THT]"]
  C5 = Electrolytic Capacitor [capacitance=10µF voltage=20V package="100 mil [THT, electrolytic]"]
  C6 = Electrolytic Capacitor [capacitance=10µF voltage=20V package="100 mil [THT, electrolytic]"]
  U7 = Optocoupler [package=THT]
  R15 = Resistor [tolerance=±5% resistance=10k package=THT]
  R16 = Resistor [tolerance=±5% resistance=330 package=THT]

nets:
  N1: Pololu_A1.ENABLE, Pololu_A2.ENABLE, U7.Pin_5, R15.Pin_0
  VDD: Pololu_A1.MS1, Pololu_A1.MS2, Pololu_A1.MS3, Pololu_A1.VDD, Pololu_A2.MS1, Pololu_A2.MS2, Pololu_A2.MS3, Pololu_A2.VDD, R1.Pin_1, R2.Pin_1, R3.Pin_1, R4.Pin_1, U6.output_voltage, C6.+, R15.Pin_1
  N2: Pololu_A1.RESET, Pololu_A1.SLEEP
  N3: Pololu_A1.STEP, U3.Pin_5, R3.Pin_0
  N4: Pololu_A1.DIR, U1.Pin_5, R1.Pin_0
  GND: Pololu_A1.GND, Pololu_A2.GND, U1.Pin_4, U2.Pin_4, U3.Pin_4, U4.Pin_4, Power_plug1.GND, S1.leg0, S2.leg0, C2.-, U6.GND, C5.-, C6.-, U7.Pin_4
  N5: Pololu_A1.1B, M1.D
  N6: Pololu_A1.1A, M1.B
  N7: Pololu_A1.2A, M1.C
  N8: Pololu_A1.2B, M1.A
  N9: Pololu_A1.VMOT, Pololu_A2.VMOT, Power_plug1.VCC, C2.+, U6.input_voltage, C5.+
  N10: Pololu_A2.RESET, Pololu_A2.SLEEP
  N11: Pololu_A2.STEP, U4.Pin_5, R4.Pin_0
  N12: Pololu_A2.DIR, U2.Pin_5, R2.Pin_0
  N13: Pololu_A2.1B, M2.D
  N14: Pololu_A2.1A, M2.B
  N15: Pololu_A2.2A, M2.C
  N16: Pololu_A2.2B, M2.A
  N17: U1.Pin_1, Part1.D6_PWM
  N18: U1.Pin_2, R5.Pin_1
  N19: U2.Pin_1, Part1.D5_PWM
  N20: U2.Pin_2, R6.Pin_1
  N21: U3.Pin_1, Part1.D3_PWM
  N22: U3.Pin_2, R7.Pin_1
  N23: U4.Pin_1, Part1.D2
  N24: U4.Pin_2, R8.Pin_1
  N25: R5.Pin_0, R6.Pin_0, R7.Pin_0, R8.Pin_0, Part1.GND, U5.pin2, S3.leg0, C4.1, C3.1, R16.Pin_0
  N26: Part1.A0, S3.leg1
  N27: Part1.D8, R12.Pin_0, U7.Pin_1
  N28: Part1.D9_PWM, R9.Pin_1, R13.Pin_0, C3.0
  N29: Part1.D10_PWM/SS, R10.Pin_1, R14.Pin_0, C4.0
  N30: Part1.D11_PWM/MOSI, U5.pin1
  N31: Part1.D12/MISO, R11.Pin_0
  N32: Part1.5V, R9.Pin_0, R12.Pin_1, R11.Pin_1, R10.Pin_0
  N33: S1.leg1, R13.Pin_1
  N34: S2.leg1, R14.Pin_1
  N35: U7.Pin_2, R16.Pin_1

notes:
  End-Stops
  OptoCop
  Allegro driver
  Laser power
  Davide Gariselli
  beta0.6 15/02/2017
  Capacitor 100nF
  Thx to Federico Altiero & Valentino Vaia
  Capacitor 10uF
  (12Vo-5Vin)*1.5A=10.5 W
  Capacitor 0.1nF
